# Fritzing sketch frtzing_sketch (saved by Fritzing 0.9.9b)
breadboards: 1

parts:
  Composant1 = Arduino MKR WiFi 1010
  Mod1 = KY-018 Photoresistor Module [package="Breakout board"]
  Mod2 = KY-018 Photoresistor Module [package="Breakout board"]  # not connected

nets:
  N1: Composant1.A6, Mod1.S

custom parts:
  Arduino MKR WiFi 1010: This is the newest version of the MKR 1000 WIFI, but with an ESP32 module on board made by U-BLOX.
  KY-018 Photoresistor Module: KY-018 Photoresistor module, used to measure light intensity. It can determine the presence or absence of light.
